# Fritzing sketch Doppler_Radar (saved by Fritzing 1.0.4)

parts:
  RCWL-0516_Microwave_Radar_Motion_Sensor1 = RCWL-0516 Microwave Radar Motion Sensor Module
  Part1 = Arduino Uno (Rev3)

nets:
  GND: RCWL-0516_Microwave_Radar_Motion_Sensor1.GND, Part1.GND
  N1: RCWL-0516_Microwave_Radar_Motion_Sensor1.OUT, Part1.D12/MISO
  VIN: RCWL-0516_Microwave_Radar_Motion_Sensor1.VIN, Part1.5V

custom parts:
  RCWL-0516 Microwave Radar Motion Sensor Module: The RCWL-0516 is a microwave radar motion sensor module. Input voltage is 4V to 28V. The 3V3 pin is a power output.
